// Logisim project 4W.circ as structural Verilog: 1 circuit, main circuit main
module main (
  input  [4:0] A_INPUT,
  input  [4:0] KEY_INPUT,
  output [3:0] out_3
);

  wire and_1_out, and_6_out, and_11_out, and_16_out, and_21_out, and_26_out, and_27_out, and_36_out,
       clock_1_out, p0, p1, p2, p3, p4, p5, p6, p7, p8, p9, p10, p11, p12, p13, p14, p15, p16, p17, p18, p19,
       p20, p21, p22, p23, p24, p25, p26, p27, p28, p29, p30, p31;
  wire [1:0] I0T0, I0T1, I0T2, I0T3, I1T0, I1T1, I1T2, I1T3, I2T0, I2T1, I2T2, I2T3, I3T0, I3T1, I3T2, I3T3,
       I4T0, I4T1, I4T2, I4T3, I5T0, I5T1, I5T2, I5T3, I6T0, I6T1, I6T2, I6T3, I7T0, I7T1, I7T2, I7T3, KT,
       or_2_out, or_3_out, or_4_out, or_5_out, or_7_out, or_8_out, or_9_out, or_10_out, or_12_out, or_13_out,
       or_14_out, or_15_out, or_17_out, or_18_out, or_19_out, or_20_out, or_22_out, or_23_out, or_24_out,
       or_25_out, or_27_out, or_28_out, or_29_out, or_30_out, or_32_out, or_33_out, or_34_out, or_35_out,
       or_37_out, or_38_out, or_39_out, or_40_out, xnor_2_out, xnor_3_out, xnor_4_out, xnor_5_out,
       xnor_6_out, xnor_7_out, xnor_9_out, xnor_10_out, xnor_11_out, xnor_12_out, xnor_14_out, xnor_15_out,
       xnor_16_out, xnor_17_out, xnor_19_out, xnor_20_out, xnor_22_out, xnor_23_out, xnor_24_out,
       xnor_25_out, xnor_27_out, xnor_28_out, xnor_29_out, xnor_30_out, xnor_32_out, xnor_33_out,
       xnor_34_out, xnor_35_out, xnor_37_out, xnor_38_out, xnor_39_out, xnor_40_out;
  wire [2:0] I0, I1, I2, I3, I4, I5, I6, I7, K, or_1_out, or_6_out, or_11_out, or_16_out, or_21_out,
       or_26_out, or_31_out, or_36_out, xnor_1_out, xnor_8_out, xnor_13_out, xnor_18_out, xnor_21_out,
       xnor_26_out, xnor_31_out, xnor_36_out;
  wire [3:0] I0D0, I0D1, I0D2, I0D3, I1D0, I1D1, I1D2, I1D3, I2D0, I2D1, I2D2, I2D3, I3D0, I3D1, I3D2, I3D3,
       I4D0, I4D1, I4D2, I4D3, I5D0, I5D1, I5D2, I5D3, I6D0, I6D1, I6D2, I6D3, I7D0, I7D1, I7D2, I7D3;
  wire [4:0] S;

  assign K = ~KEY_INPUT[4:2];  // NOT_Gate not_1, 3 bits wide
  assign KT = ~KEY_INPUT[1:0];  // NOT_Gate not_2, 2 bits wide
  Clock clock_1 (.out(clock_1_out));
  Priority_Encoder #(.select(5)) priority_encoder_1 (
    .in0(p0), .in1(p1), .in2(p2), .in3(p3), .in4(p4), .in5(p5), .in6(p6), .in7(p7), .in8(p8), .in9(p9),
    .in10(p10), .in11(p11), .in12(p12), .in13(p13), .in14(p14), .in15(p15), .in16(p16), .in17(p17),
    .in18(p18), .in19(p19), .in20(p20), .in21(p21), .in22(p22), .in23(p23), .in24(p24), .in25(p25),
    .in26(p26), .in27(p27), .in28(p28), .in29(p29), .in30(p30), .in31(p31), .out(S));  // open: gs, en_out, en_in
  Shift_Register #(.length(3)) shift_register_1 (
    .shift(1'b0), .in(1'b0), .clk(clock_1_out), .q0(I0[2]), .q1(I0[1]), .q2(I0[0]));  // open: out, load, clr, d0, d1, d2
  Shift_Register #(.length(3)) shift_register_2 (
    .shift(1'b0), .in(1'b0), .clk(clock_1_out), .q0(I1[2]), .q1(I1[1]), .q2(I1[0]));  // open: out, load, clr, d0, d1, d2
  Shift_Register #(.length(3)) shift_register_3 (
    .shift(1'b0), .in(1'b0), .clk(clock_1_out), .q0(I2[2]), .q1(I2[1]), .q2(I2[0]));  // open: out, load, clr, d0, d1, d2
  Shift_Register #(.length(3)) shift_register_4 (
    .shift(1'b0), .in(1'b0), .clk(clock_1_out), .q0(I3[2]), .q1(I3[1]), .q2(I3[0]));  // open: out, load, clr, d0, d1, d2
  Multiplexer #(.select(5), .width(4), .enable("false")) multiplexer_1 (
    .in0(I0D0), .in1(I0D1), .in2(I0D2), .in3(I0D3), .in4(I1D0), .in5(I1D1), .in6(I1D2), .in7(I1D3),
    .in8(I2D0), .in9(I2D1), .in10(I2D2), .in11(I2D3), .in12(I3D0), .in13(I3D1), .in14(I3D2), .in15(I3D3),
    .in16(I4D0), .in17(I4D1), .in18(I4D2), .in19(I4D3), .in20(I5D0), .in21(I5D1), .in22(I5D2), .in23(I5D3),
    .in24(I6D0), .in25(I6D1), .in26(I6D2), .in27(I6D3), .in28(I7D0), .in29(I7D1), .in30(I7D2), .in31(I7D3),
    .out(out_3), .sel(S));
  Shift_Register #(.length(24)) shift_register_5 (
    .shift(1'b0), .in(1'b0), .clk(clock_1_out), .q0(I0T0[1]), .q1(I0T0[0]), .q2(I0D0[3]), .q3(I0D0[2]),
    .q4(I0D0[1]), .q5(I0D0[0]), .q6(I0T1[1]), .q7(I0T1[0]), .q8(I0D1[3]), .q9(I0D1[2]), .q10(I0D1[1]),
    .q11(I0D1[0]), .q12(I0T2[1]), .q13(I0T2[0]), .q14(I0D2[3]), .q15(I0D2[2]), .q16(I0D2[1]), .q17(I0D2[0]),
    .q18(I0T3[1]), .q19(I0T3[0]), .q20(I0D3[3]), .q21(I0D3[2]), .q22(I0D3[1]), .q23(I0D3[0]));  // open: out, load, clr, d0, d1, d2, d3, d4, d5, d6, d7, d8, d9, d10, d11, d12, d13, d14, d15, d16, d17, d18, d19, d20, d21, d22, d23
  Shift_Register #(.length(24)) shift_register_6 (
    .shift(1'b0), .in(1'b0), .clk(clock_1_out), .q0(I1T0[1]), .q1(I1T0[0]), .q2(I1D0[3]), .q3(I1D0[2]),
    .q4(I1D0[1]), .q5(I1D0[0]), .q6(I1T1[1]), .q7(I1T1[0]), .q8(I1D1[3]), .q9(I1D1[2]), .q10(I1D1[1]),
    .q11(I1D1[0]), .q12(I1T2[1]), .q13(I1T2[0]), .q14(I1D2[3]), .q15(I1D2[2]), .q16(I1D2[1]), .q17(I1D2[0]),
    .q18(I1T3[1]), .q19(I1T3[0]), .q20(I1D3[3]), .q21(I1D3[2]), .q22(I1D3[1]), .q23(I1D3[0]));  // open: out, load, clr, d0, d1, d2, d3, d4, d5, d6, d7, d8, d9, d10, d11, d12, d13, d14, d15, d16, d17, d18, d19, d20, d21, d22, d23
  Shift_Register #(.length(3)) shift_register_7 (
    .shift(1'b0), .in(1'b0), .clk(clock_1_out), .q0(I4[2]), .q1(I4[1]), .q2(I4[0]));  // open: out, load, clr, d0, d1, d2
  Shift_Register #(.length(3)) shift_register_8 (
    .shift(1'b0), .in(1'b0), .clk(clock_1_out), .q0(I5[2]), .q1(I5[1]), .q2(I5[0]));  // open: out, load, clr, d0, d1, d2
  Shift_Register #(.length(3)) shift_register_9 (
    .shift(1'b0), .in(1'b0), .clk(clock_1_out), .q0(I6[2]), .q1(I6[1]), .q2(I6[0]));  // open: out, load, clr, d0, d1, d2
  Shift_Register #(.length(3)) shift_register_10 (
    .shift(1'b0), .in(1'b0), .clk(clock_1_out), .q0(I7[2]), .q1(I7[1]), .q2(I7[0]));  // open: out, load, clr, d0, d1, d2
  Shift_Register #(.length(24)) shift_register_11 (
    .shift(1'b0), .in(1'b0), .clk(clock_1_out), .q0(I2T0[1]), .q1(I2T0[0]), .q2(I2D0[3]), .q3(I2D0[2]),
    .q4(I2D0[1]), .q5(I2D0[0]), .q6(I2T1[1]), .q7(I2T1[0]), .q8(I2D1[3]), .q9(I2D1[2]), .q10(I2D1[1]),
    .q11(I2D1[0]), .q12(I2T2[1]), .q13(I2T2[0]), .q14(I2D2[3]), .q15(I2D2[2]), .q16(I2D2[1]), .q17(I2D2[0]),
    .q18(I2T3[1]), .q19(I2T3[0]), .q20(I2D3[3]), .q21(I2D3[2]), .q22(I2D3[1]), .q23(I2D3[0]));  // open: out, load, clr, d0, d1, d2, d3, d4, d5, d6, d7, d8, d9, d10, d11, d12, d13, d14, d15, d16, d17, d18, d19, d20, d21, d22, d23
  Shift_Register #(.length(24)) shift_register_12 (
    .shift(1'b0), .in(1'b0), .clk(clock_1_out), .q0(I3T0[1]), .q1(I3T0[0]), .q2(I3D0[3]), .q3(I3D0[2]),
    .q4(I3D0[1]), .q5(I3D0[0]), .q6(I3T1[1]), .q7(I3T1[0]), .q8(I3D1[3]), .q9(I3D1[2]), .q10(I3D1[1]),
    .q11(I3D1[0]), .q12(I3T2[1]), .q13(I3T2[0]), .q14(I3D2[3]), .q15(I3D2[2]), .q16(I3D2[1]), .q17(I3D2[0]),
    .q18(I3T3[1]), .q19(I3T3[0]), .q20(I3D3[3]), .q21(I3D3[2]), .q22(I3D3[1]), .q23(I3D3[0]));  // open: out, load, clr, d0, d1, d2, d3, d4, d5, d6, d7, d8, d9, d10, d11, d12, d13, d14, d15, d16, d17, d18, d19, d20, d21, d22, d23
  Shift_Register #(.length(24)) shift_register_13 (
    .shift(1'b0), .in(1'b0), .clk(clock_1_out), .q0(I4T0[1]), .q1(I4T0[0]), .q2(I4D0[3]), .q3(I4D0[2]),
    .q4(I4D0[1]), .q5(I4D0[0]), .q6(I4T1[1]), .q7(I4T1[0]), .q8(I4D1[3]), .q9(I4D1[2]), .q10(I4D1[1]),
    .q11(I4D1[0]), .q12(I4T2[1]), .q13(I4T2[0]), .q14(I4D2[3]), .q15(I4D2[2]), .q16(I4D2[1]), .q17(I4D2[0]),
    .q18(I4T3[1]), .q19(I4T3[0]), .q20(I4D3[3]), .q21(I4D3[2]), .q22(I4D3[1]), .q23(I4D3[0]));  // open: out, load, clr, d0, d1, d2, d3, d4, d5, d6, d7, d8, d9, d10, d11, d12, d13, d14, d15, d16, d17, d18, d19, d20, d21, d22, d23
  Shift_Register #(.length(24)) shift_register_14 (
    .shift(1'b0), .in(1'b0), .clk(clock_1_out), .q0(I5T0[1]), .q1(I5T0[0]), .q2(I5D0[3]), .q3(I5D0[2]),
    .q4(I5D0[1]), .q5(I5D0[0]), .q6(I5T1[1]), .q7(I5T1[0]), .q8(I5D1[3]), .q9(I5D1[2]), .q10(I5D1[1]),
    .q11(I5D1[0]), .q12(I5T2[1]), .q13(I5T2[0]), .q14(I5D2[3]), .q15(I5D2[2]), .q16(I5D2[1]), .q17(I5D2[0]),
    .q18(I5T3[1]), .q19(I5T3[0]), .q20(I5D3[3]), .q21(I5D3[2]), .q22(I5D3[1]), .q23(I5D3[0]));  // open: out, load, clr, d0, d1, d2, d3, d4, d5, d6, d7, d8, d9, d10, d11, d12, d13, d14, d15, d16, d17, d18, d19, d20, d21, d22, d23
  Shift_Register #(.length(24)) shift_register_15 (
    .shift(1'b0), .in(1'b0), .clk(clock_1_out), .q0(I6T0[1]), .q1(I6T0[0]), .q2(I6D0[3]), .q3(I6D0[2]),
    .q4(I6D0[1]), .q5(I6D0[0]), .q6(I6T1[1]), .q7(I6T1[0]), .q8(I6D1[3]), .q9(I6D1[2]), .q10(I6D1[1]),
    .q11(I6D1[0]), .q12(I6T2[1]), .q13(I6T2[0]), .q14(I6D2[3]), .q15(I6D2[2]), .q16(I6D2[1]), .q17(I6D2[0]),
    .q18(I6T3[1]), .q19(I6T3[0]), .q20(I6D3[3]), .q21(I6D3[2]), .q22(I6D3[1]), .q23(I6D3[0]));  // open: out, load, clr, d0, d1, d2, d3, d4, d5, d6, d7, d8, d9, d10, d11, d12, d13, d14, d15, d16, d17, d18, d19, d20, d21, d22, d23
  Shift_Register #(.length(24)) shift_register_16 (
    .shift(1'b0), .in(1'b0), .clk(clock_1_out), .q0(I7T0[1]), .q1(I7T0[0]), .q2(I7D0[3]), .q3(I7D0[2]),
    .q4(I7D0[1]), .q5(I7D0[0]), .q6(I7T1[1]), .q7(I7T1[0]), .q8(I7D1[3]), .q9(I7D1[2]), .q10(I7D1[1]),
    .q11(I7D1[0]), .q12(I7T2[1]), .q13(I7T2[0]), .q14(I7D2[3]), .q15(I7D2[2]), .q16(I7D2[1]), .q17(I7D2[0]),
    .q18(I7T3[1]), .q19(I7T3[0]), .q20(I7D3[3]), .q21(I7D3[2]), .q22(I7D3[1]), .q23(I7D3[0]));  // open: out, load, clr, d0, d1, d2, d3, d4, d5, d6, d7, d8, d9, d10, d11, d12, d13, d14, d15, d16, d17, d18, d19, d20, d21, d22, d23
  assign xnor_1_out = ~(A_INPUT[4:2] ^ I1);  // XNOR_Gate xnor_1, 3 bits wide
  assign xnor_2_out = ~(A_INPUT[1:0] ^ I1T0);  // XNOR_Gate xnor_2, 2 bits wide
  assign xnor_3_out = ~(A_INPUT[1:0] ^ I1T1);  // XNOR_Gate xnor_3, 2 bits wide
  assign xnor_4_out = ~(I1T2 ^ A_INPUT[1:0]);  // XNOR_Gate xnor_4, 2 bits wide
  assign xnor_5_out = ~(A_INPUT[1:0] ^ I1T3);  // XNOR_Gate xnor_5, 2 bits wide
  assign xnor_6_out = ~(A_INPUT[1:0] ^ I0T0);  // XNOR_Gate xnor_6, 2 bits wide
  assign xnor_7_out = ~(A_INPUT[1:0] ^ I0T1);  // XNOR_Gate xnor_7, 2 bits wide
  assign xnor_8_out = ~(A_INPUT[4:2] ^ I2);  // XNOR_Gate xnor_8, 3 bits wide
  assign xnor_9_out = ~(A_INPUT[1:0] ^ I2T0);  // XNOR_Gate xnor_9, 2 bits wide
  assign xnor_10_out = ~(A_INPUT[1:0] ^ I2T1);  // XNOR_Gate xnor_10, 2 bits wide
  assign xnor_11_out = ~(I2T2 ^ A_INPUT[1:0]);  // XNOR_Gate xnor_11, 2 bits wide
  assign xnor_12_out = ~(A_INPUT[1:0] ^ I2T3);  // XNOR_Gate xnor_12, 2 bits wide
  assign xnor_13_out = ~(A_INPUT[4:2] ^ I3);  // XNOR_Gate xnor_13, 3 bits wide
  assign xnor_14_out = ~(A_INPUT[1:0] ^ I3T0);  // XNOR_Gate xnor_14, 2 bits wide
  assign xnor_15_out = ~(A_INPUT[1:0] ^ I3T1);  // XNOR_Gate xnor_15, 2 bits wide
  assign xnor_16_out = ~(I3T2 ^ A_INPUT[1:0]);  // XNOR_Gate xnor_16, 2 bits wide
  assign xnor_17_out = ~(A_INPUT[1:0] ^ I3T3);  // XNOR_Gate xnor_17, 2 bits wide
  assign or_1_out = xnor_1_out | K;  // OR_Gate or_1, 3 bits wide
  assign or_2_out = xnor_2_out | KT;  // OR_Gate or_2, 2 bits wide
  assign or_3_out = xnor_3_out | KT;  // OR_Gate or_3, 2 bits wide
  assign or_4_out = xnor_4_out | KT;  // OR_Gate or_4, 2 bits wide
  assign or_5_out = xnor_5_out | KT;  // OR_Gate or_5, 2 bits wide
  assign xnor_18_out = ~(A_INPUT[4:2] ^ I0);  // XNOR_Gate xnor_18, 3 bits wide
  assign or_6_out = xnor_18_out | K;  // OR_Gate or_6, 3 bits wide
  assign or_7_out = xnor_6_out | KT;  // OR_Gate or_7, 2 bits wide
  assign or_8_out = xnor_7_out | KT;  // OR_Gate or_8, 2 bits wide
  assign xnor_19_out = ~(I0T2 ^ A_INPUT[1:0]);  // XNOR_Gate xnor_19, 2 bits wide
  assign or_9_out = xnor_19_out | KT;  // OR_Gate or_9, 2 bits wide
  assign or_10_out = xnor_20_out | KT;  // OR_Gate or_10, 2 bits wide
  assign xnor_20_out = ~(A_INPUT[1:0] ^ I0T3);  // XNOR_Gate xnor_20, 2 bits wide
  assign or_11_out = xnor_8_out | K;  // OR_Gate or_11, 3 bits wide
  assign or_12_out = xnor_9_out | KT;  // OR_Gate or_12, 2 bits wide
  assign or_13_out = xnor_10_out | KT;  // OR_Gate or_13, 2 bits wide
  assign or_14_out = xnor_11_out | KT;  // OR_Gate or_14, 2 bits wide
  assign or_15_out = xnor_12_out | KT;  // OR_Gate or_15, 2 bits wide
  assign or_16_out = xnor_13_out | K;  // OR_Gate or_16, 3 bits wide
  assign or_17_out = xnor_14_out | KT;  // OR_Gate or_17, 2 bits wide
  assign or_18_out = xnor_15_out | KT;  // OR_Gate or_18, 2 bits wide
  assign or_19_out = xnor_16_out | KT;  // OR_Gate or_19, 2 bits wide
  assign or_20_out = xnor_17_out | KT;  // OR_Gate or_20, 2 bits wide
  and and_1 (and_1_out, or_1_out[0], or_1_out[1], or_1_out[2]);
  and and_2 (p4, or_2_out[0], or_2_out[1], and_1_out);
  and and_3 (p5, or_3_out[0], or_3_out[1], and_1_out);
  and and_4 (p6, or_4_out[0], or_4_out[1], and_1_out);
  and and_5 (p7, or_5_out[0], or_5_out[1], and_1_out);
  and and_6 (and_6_out, or_6_out[0], or_6_out[1], or_6_out[2]);
  and and_7 (p0, or_7_out[0], or_7_out[1], and_6_out);
  and and_8 (p1, or_8_out[0], or_8_out[1], and_6_out);
  and and_9 (p2, or_9_out[0], or_9_out[1], and_6_out);
  and and_10 (p3, or_10_out[0], or_10_out[1], and_6_out);
  and and_11 (and_11_out, or_11_out[0], or_11_out[1], or_11_out[2]);
  and and_12 (p8, or_12_out[0], or_12_out[1], and_11_out);
  and and_13 (p9, or_13_out[0], or_13_out[1], and_11_out);
  and and_14 (p10, or_14_out[0], or_14_out[1], and_11_out);
  and and_15 (p11, or_15_out[0], or_15_out[1], and_11_out);
  and and_16 (and_16_out, or_16_out[0], or_16_out[1], or_16_out[2]);
  and and_17 (p12, or_17_out[0], or_17_out[1], and_16_out);
  and and_18 (p13, or_18_out[0], or_18_out[1], and_16_out);
  and and_19 (p14, or_19_out[0], or_19_out[1], and_16_out);
  and and_20 (p15, or_20_out[0], or_20_out[1], and_16_out);
  assign xnor_21_out = ~(A_INPUT[4:2] ^ I7);  // XNOR_Gate xnor_21, 3 bits wide
  assign xnor_22_out = ~(A_INPUT[1:0] ^ I7T0);  // XNOR_Gate xnor_22, 2 bits wide
  assign xnor_23_out = ~(A_INPUT[1:0] ^ I7T1);  // XNOR_Gate xnor_23, 2 bits wide
  assign xnor_24_out = ~(I7T2 ^ A_INPUT[1:0]);  // XNOR_Gate xnor_24, 2 bits wide
  assign xnor_25_out = ~(A_INPUT[1:0] ^ I7T3);  // XNOR_Gate xnor_25, 2 bits wide
  assign or_21_out = xnor_21_out | K;  // OR_Gate or_21, 3 bits wide
  assign or_22_out = xnor_22_out | KT;  // OR_Gate or_22, 2 bits wide
  assign or_23_out = xnor_23_out | KT;  // OR_Gate or_23, 2 bits wide
  assign or_24_out = xnor_24_out | KT;  // OR_Gate or_24, 2 bits wide
  assign or_25_out = xnor_25_out | KT;  // OR_Gate or_25, 2 bits wide
  assign xnor_26_out = ~(A_INPUT[4:2] ^ I6);  // XNOR_Gate xnor_26, 3 bits wide
  assign or_26_out = xnor_26_out | K;  // OR_Gate or_26, 3 bits wide
  assign xnor_27_out = ~(A_INPUT[1:0] ^ I6T0);  // XNOR_Gate xnor_27, 2 bits wide
  assign xnor_28_out = ~(A_INPUT[1:0] ^ I6T1);  // XNOR_Gate xnor_28, 2 bits wide
  assign xnor_29_out = ~(I6T2 ^ A_INPUT[1:0]);  // XNOR_Gate xnor_29, 2 bits wide
  assign xnor_30_out = ~(A_INPUT[1:0] ^ I6T3);  // XNOR_Gate xnor_30, 2 bits wide
  assign xnor_31_out = ~(A_INPUT[4:2] ^ I5);  // XNOR_Gate xnor_31, 3 bits wide
  assign xnor_32_out = ~(A_INPUT[1:0] ^ I5T0);  // XNOR_Gate xnor_32, 2 bits wide
  assign xnor_33_out = ~(A_INPUT[1:0] ^ I5T1);  // XNOR_Gate xnor_33, 2 bits wide
  assign xnor_34_out = ~(I5T2 ^ A_INPUT[1:0]);  // XNOR_Gate xnor_34, 2 bits wide
  assign xnor_35_out = ~(A_INPUT[1:0] ^ I5T3);  // XNOR_Gate xnor_35, 2 bits wide
  assign xnor_36_out = ~(A_INPUT[4:2] ^ I4);  // XNOR_Gate xnor_36, 3 bits wide
  assign xnor_37_out = ~(A_INPUT[1:0] ^ I4T0);  // XNOR_Gate xnor_37, 2 bits wide
  assign xnor_38_out = ~(A_INPUT[1:0] ^ I4T1);  // XNOR_Gate xnor_38, 2 bits wide
  assign xnor_39_out = ~(I4T2 ^ A_INPUT[1:0]);  // XNOR_Gate xnor_39, 2 bits wide
  assign xnor_40_out = ~(A_INPUT[1:0] ^ I4T3);  // XNOR_Gate xnor_40, 2 bits wide
  and and_21 (and_21_out, or_21_out[0], or_21_out[1], or_21_out[2]);
  and and_22 (p28, or_22_out[0], or_22_out[1], and_21_out);
  and and_23 (p29, or_23_out[0], or_23_out[1], and_21_out);
  and and_24 (p30, or_24_out[0], or_24_out[1], and_21_out);
  and and_25 (p31, or_25_out[0], or_25_out[1], and_21_out);
  and and_26 (and_26_out, or_26_out[0], or_26_out[1], or_26_out[2]);
  assign or_27_out = xnor_27_out | KT;  // OR_Gate or_27, 2 bits wide
  assign or_28_out = xnor_28_out | KT;  // OR_Gate or_28, 2 bits wide
  assign or_29_out = xnor_29_out | KT;  // OR_Gate or_29, 2 bits wide
  assign or_30_out = xnor_30_out | KT;  // OR_Gate or_30, 2 bits wide
  and and_27 (and_27_out, or_31_out[0], or_31_out[1], or_31_out[2]);
  assign or_31_out = xnor_31_out | K;  // OR_Gate or_31, 3 bits wide
  assign or_32_out = xnor_32_out | KT;  // OR_Gate or_32, 2 bits wide
  assign or_33_out = xnor_33_out | KT;  // OR_Gate or_33, 2 bits wide
  assign or_34_out = xnor_34_out | KT;  // OR_Gate or_34, 2 bits wide
  assign or_35_out = xnor_35_out | KT;  // OR_Gate or_35, 2 bits wide
  assign or_36_out = xnor_36_out | K;  // OR_Gate or_36, 3 bits wide
  assign or_37_out = xnor_37_out | KT;  // OR_Gate or_37, 2 bits wide
  assign or_38_out = xnor_38_out | KT;  // OR_Gate or_38, 2 bits wide
  assign or_39_out = xnor_39_out | KT;  // OR_Gate or_39, 2 bits wide
  assign or_40_out = xnor_40_out | KT;  // OR_Gate or_40, 2 bits wide
  and and_28 (p24, or_27_out[0], or_27_out[1], and_26_out);
  and and_29 (p25, or_28_out[0], or_28_out[1], and_26_out);
  and and_30 (p26, or_29_out[0], or_29_out[1], and_26_out);
  and and_31 (p27, or_30_out[0], or_30_out[1], and_26_out);
  and and_32 (p20, or_32_out[0], or_32_out[1], and_27_out);
  and and_33 (p21, or_33_out[0], or_33_out[1], and_27_out);
  and and_34 (p22, or_34_out[0], or_34_out[1], and_27_out);
  and and_35 (p23, or_35_out[0], or_35_out[1], and_27_out);
  and and_36 (and_36_out, or_36_out[0], or_36_out[1], or_36_out[2]);
  and and_37 (p16, or_37_out[0], or_37_out[1], and_36_out);
  and and_38 (p17, or_38_out[0], or_38_out[1], and_36_out);
  and and_39 (p18, or_39_out[0], or_39_out[1], and_36_out);
  and and_40 (p19, or_40_out[0], or_40_out[1], and_36_out);

  // Other names for the same wires on the sheet: A[2:0] = A_INPUT[4:2]; AT[1:0] = A_INPUT[1:0]

  // Notes on the sheet:
  //   I0 A EXNOR KBAR SATHE OR
endmodule
