// Logisim project COINNOVATIVE108120.circ as structural Verilog: 1 circuit, main circuit main
module main (
  input  [3:0] Enter_Number_of_Quantity,
  input  [4:0] in_2,
  input  in_3,
  input  c,
  output [3:0] out_5,
  output [7:0] out_6,
  output [7:0] out_7
);

  wire aa, adder_2_cout, and_9_out, and_18_out, and_19_out, and_20_out, and_21_out, and_22_out, and_23_out,
       and_24_out, and_25_out, and_26_out, and_27_out, and_28_out, and_29_out, and_30_out, and_31_out,
       and_32_out, and_33_out, and_34_out, and_35_out, and_36_out, bb, cc, clock_1_out, co1, co2,
       counter_1_q, d_ff_1_q, dd, deco, decoder_1_out0, ee, ff, gg, not_1_out, not_2_out, not_3_out,
       not_4_out, or_1_out, or_2_out, or_7_out, r1, r2, r3, r4, xor_1_out;
  wire [2:0] and_15_out;
  wire [3:0] add2, add3, add4;
  wire [3:1] ans1, ans2;
  wire [4:0] Enter_product_id_q;
  wire [7:0] adder_2_out, B_q7;

  Clock clock_1 (.out(clock_1_out));
  Decoder decoder_1 (.out0(decoder_1_out0), .out1(deco), .sel(counter_1_q));  // open: en
  Counter #(.width(1), .max('h1)) counter_1 (.Q(counter_1_q), .clk(clock_1_out));  // open: load, D, count, carry, clr
  Counter #(.width(5), .max('h1f)) Enter_product_id (
    .count(c), .Q(Enter_product_id_q), .clk(decoder_1_out0));  // open: load, D, carry, clr
  and and_1 (add4[3], out_5[3], Enter_Number_of_Quantity[3]);
  and and_2 (add4[2], out_5[2], Enter_Number_of_Quantity[3]);
  _4W_main main_1 (.A_INPUT(Enter_product_id_q), .KEY_INPUT(in_2), .out_3(out_5));
  and and_3 (add3[3], out_5[3], Enter_Number_of_Quantity[2]);
  and and_4 (add4[1], out_5[1], Enter_Number_of_Quantity[3]);
  and and_5 (add2[3], out_5[3], Enter_Number_of_Quantity[1]);
  and and_6 (add3[2], out_5[2], Enter_Number_of_Quantity[2]);
  and and_7 (add4[0], out_5[0], Enter_Number_of_Quantity[3]);
  Shift_Register A__Ans (
    .shift(1'b0), .clk(clock_1_out), .load(deco), .clr(in_3), .d0(adder_2_out[7]), .q0(out_6[7]),
    .d1(adder_2_out[6]), .q1(out_6[6]), .d2(adder_2_out[5]), .q2(out_6[5]), .d3(adder_2_out[4]),
    .q3(out_6[4]), .d4(adder_2_out[3]), .q4(out_6[3]), .d5(adder_2_out[2]), .q5(out_6[2]),
    .d6(adder_2_out[1]), .q6(out_6[1]), .d7(adder_2_out[0]), .q7(out_6[0]));  // open: in, out
  Shift_Register B (
    .shift(1'b0), .clk(clock_1_out), .load(or_1_out), .clr(in_3), .d0(out_7[7]), .q0(B_q7[7]), .d1(out_7[6]),
    .q1(B_q7[6]), .d2(out_7[5]), .q2(B_q7[5]), .d3(out_7[4]), .q3(B_q7[4]), .d4(out_7[3]), .q4(B_q7[3]),
    .d5(out_7[2]), .q5(B_q7[2]), .d6(out_7[1]), .q6(B_q7[1]), .d7(out_7[0]), .q7(B_q7[0]));  // open: in, out
  and and_8 (and_15_out[2], out_5[3], Enter_Number_of_Quantity[0]);
  Adder #(.width(4)) adder_1 (.a({co2, ans2}), .b(add4), .out(out_7[6:3]), .cout(out_7[7]));  // open: cin
  and and_9 (and_9_out, deco, clock_1_out);
  Counter #(.width(4), .max('h9)) Number_of_items (
    .load(c), .count(decoder_1_out0), .Q({r1, r2, r3, r4}), .clk(decoder_1_out0));  // open: D, carry, clr
  and and_10 (add2[2], out_5[2], Enter_Number_of_Quantity[1]);
  and and_11 (add3[1], out_5[1], Enter_Number_of_Quantity[2]);
  and and_12 (and_15_out[1], out_5[2], Enter_Number_of_Quantity[0]);
  and and_13 (add2[1], out_5[1], Enter_Number_of_Quantity[1]);
  and and_14 (add3[0], out_5[0], Enter_Number_of_Quantity[2]);
  Adder adder_2 (.a(out_6), .b(B_q7), .out(adder_2_out), .cin(d_ff_1_q), .cout(adder_2_cout));
  D_Flip_Flop d_ff_1 (.clk(and_9_out), .D(adder_2_cout), .Q(d_ff_1_q));  // open: Qn, preset, en, reset
  and and_15 (and_15_out[0], out_5[1], Enter_Number_of_Quantity[0]);
  Adder #(.width(4)) adder_3 (.a({1'b0, and_15_out}), .b(add2), .out({ans1, out_7[1]}), .cout(co1));  // open: cin
  and and_16 (add2[0], out_5[0], Enter_Number_of_Quantity[1]);
  Adder #(.width(4)) adder_4 (.a({co1, ans1}), .b(add3), .out({ans2, out_7[2]}), .cout(co2));  // open: cin
  _7_Segment_Display u_7_segment_display_1 (.g(gg), .f(ff), .a(aa), .b(bb), .e(ee), .d(dd), .c(cc), .dp(1'b1));
  and and_17 (out_7[0], out_5[0], Enter_Number_of_Quantity[0]);
  or or_1 (or_1_out, out_7[7], out_7[6], out_7[5], out_7[4], out_7[3], out_7[2], out_7[1], out_7[0]);
  not not_1 (not_1_out, r1);
  not not_2 (not_2_out, r2);
  not not_3 (not_3_out, r3);
  not not_4 (not_4_out, r4);
  and and_18 (and_18_out, r2, r4);
  xor xor_1 (xor_1_out, r1, r2);
  or or_2 (or_2_out, and_18_out, r3);
  and and_19 (and_19_out, not_2_out, not_3_out, not_4_out);
  and and_20 (and_20_out, not_1_out, not_2_out, r3);
  and and_21 (and_21_out, not_4_out, not_1_out, r3);
  and and_22 (and_22_out, not_1_out, r2, not_3_out, r4);
  and and_23 (and_23_out, not_1_out, r3, not_4_out);
  and and_24 (and_24_out, xor_1_out, not_3_out);
  and and_25 (and_25_out, not_1_out, not_3_out, not_4_out);
  and and_26 (and_26_out, not_1_out, not_4_out, r2);
  and and_27 (and_27_out, not_1_out, r3);
  and and_28 (and_28_out, not_2_out, not_3_out);
  and and_29 (and_29_out, not_1_out, r2);
  and and_30 (and_30_out, not_1_out, r4);
  and and_31 (and_31_out, not_2_out, not_3_out);
  and and_32 (and_32_out, not_1_out, or_2_out);
  or or_3 (ee, and_19_out, and_23_out);
  or or_4 (ff, and_24_out, and_25_out, and_26_out);
  or or_5 (gg, and_24_out, and_27_out);
  or or_6 (cc, and_28_out, and_29_out, and_30_out);
  and and_33 (and_33_out, r4, not_1_out, r3);
  and and_34 (and_34_out, not_1_out, not_2_out);
  and and_35 (and_35_out, not_2_out, not_3_out);
  or or_7 (or_7_out, r1, not_4_out);
  or or_8 (dd, and_19_out, and_20_out, and_21_out, and_22_out);
  and and_36 (and_36_out, or_7_out, and_31_out);
  or or_9 (bb, and_33_out, and_34_out, and_35_out);
  or or_10 (aa, and_32_out, and_36_out);

  // Other names for the same wires on the sheet: Ans[7:0] = out_6; as1[3:0] = out_5; clr = in_3; ou2[7:0] = out_7;
  //   ans1[0] = out_7[1]; ans2[0] = out_7[2]; Q[3:0] = Enter_Number_of_Quantity; B1 = Enter_Number_of_Quantity[1];
  //   B2 = Enter_Number_of_Quantity[2]; B3 = Enter_Number_of_Quantity[3]

  // Notes on the sheet:
  //   CO INNOVATIVE
  //   Total Amount
  //   No. of products
  //   MADE BY: NISHITA SHAH(15BCE108)
  //   MEERA SUTHAR(15BCE120)
endmodule
